// Logisim project proyecto.circ as structural Verilog
module Registro_32_bits (
  input  [31:0] Entrada_Bus_C,
  input  LOAD,
  input  CLK,
  output [31:0] Salida
);

  wire [31:0] multiplexer_1_out;

  Multiplexer #(.width(32)) multiplexer_1 (.in0(Salida), .in1(Entrada_Bus_C), .out(multiplexer_1_out), .sel(LOAD));
  Register #(.width(32)) register_1 (.D(multiplexer_1_out), .clk(CLK), .Q(Salida));  // open: en, clr
endmodule

module Data_Path (
  input  [31:0] Entrada_Bus_C,
  input  Enable_MDR,
  input  Enable_PC,
  input  [7:0] Entrada_MBR,
  input  Enable_MBR_Signo,
  input  Enable_MBRU,
  input  Enable_SP,
  input  Enable_LV,
  input  Enable_CPP,
  input  Enable_TOS,
  input  Enable_OPC,
  output [31:0] Salida_MAR,
  output [31:0] Salida_MDR_Memoria,
  output [31:0] Salida_PC_Memoria,
  output [31:0] Bus_B,
  output [31:0] Salida_H
);

  wire [31:0] CPP_salida, LV_salida, mbr_1_salida_mbr_signo, mbr_1_salida_mbru, MDR_salida, OPC_salida,
       PC_salida, SP_salida, TOS_salida;

  Registro_32_bits MAR (.Entrada_Bus_C(Entrada_Bus_C), .Salida(Salida_MAR));  // open: LOAD, CLK
  Registro_32_bits MDR (.Entrada_Bus_C(Entrada_Bus_C), .Salida(MDR_salida));  // open: LOAD, CLK
  Registro_32_bits PC (.Entrada_Bus_C(Entrada_Bus_C), .Salida(PC_salida));  // open: LOAD, CLK
  MBR mbr_1 (
    .Entrada_Memoria(Entrada_MBR), .Salida_MBR_Signo(mbr_1_salida_mbr_signo), .Salida_MBRU(mbr_1_salida_mbru));  // open: LOAD_MBR, CLK
  Registro_32_bits SP (.Entrada_Bus_C(Entrada_Bus_C), .Salida(SP_salida));  // open: LOAD, CLK
  Registro_32_bits LV (.Entrada_Bus_C(Entrada_Bus_C), .Salida(LV_salida));  // open: LOAD, CLK
  Registro_32_bits CPP (.Entrada_Bus_C(Entrada_Bus_C), .Salida(CPP_salida));  // open: LOAD, CLK
  Registro_32_bits TOS (.Entrada_Bus_C(Entrada_Bus_C), .Salida(TOS_salida));  // open: LOAD, CLK
  Registro_32_bits OPC (.Entrada_Bus_C(Entrada_Bus_C), .Salida(OPC_salida));  // open: LOAD, CLK
  Registro_32_bits H (.Entrada_Bus_C(Entrada_Bus_C), .Salida(Salida_H));  // open: LOAD, CLK
  assign Bus_B = Enable_MDR ? MDR_salida : 32'bz;  // Controlled_Buffer controlled_buffer_1
  assign Bus_B = Enable_PC ? PC_salida : 32'bz;  // Controlled_Buffer controlled_buffer_2
  assign Bus_B = Enable_MBR_Signo ? mbr_1_salida_mbr_signo : 32'bz;  // Controlled_Buffer controlled_buffer_3
  assign Bus_B = Enable_MBRU ? mbr_1_salida_mbru : 32'bz;  // Controlled_Buffer controlled_buffer_4
  assign Bus_B = Enable_SP ? SP_salida : 32'bz;  // Controlled_Buffer controlled_buffer_5
  assign Bus_B = Enable_LV ? LV_salida : 32'bz;  // Controlled_Buffer controlled_buffer_6
  assign Bus_B = Enable_CPP ? CPP_salida : 32'bz;  // Controlled_Buffer controlled_buffer_7
  assign Bus_B = Enable_TOS ? TOS_salida : 32'bz;  // Controlled_Buffer controlled_buffer_8
  assign Bus_B = Enable_OPC ? OPC_salida : 32'bz;  // Controlled_Buffer controlled_buffer_9

  assign Salida_MDR_Memoria = Bus_B;
  assign Salida_PC_Memoria = Bus_B;

  // Notes on the sheet:
  //   Conectar Entrada_Bus_C a la salida del Shifter
  //   Puntos de conexion
  //   Conectar Bus B a la entrada B de la ALU
  //   Conectar Salida_H a la entrada A de la ALU
  //   Salidas MAR/MDR/PC: Conectar a los puertos de la memoria principal.
  //   BORRAR TODOS LOS TEXTOS EN NEGRO QUE PUSE CUANDO TERMINEN, LOS PUSE PARA QUE SE GUIEN
endmodule

module Registro_8_bits (
  input  [7:0] Entrada_Bus_C,
  input  LOAD,
  input  CLK,
  output [7:0] Salida
);

  wire [7:0] multiplexer_1_out;

  Multiplexer #(.width(8)) multiplexer_1 (.in0(Salida), .in1(Entrada_Bus_C), .out(multiplexer_1_out), .sel(LOAD));
  Register register_1 (.D(multiplexer_1_out), .clk(CLK), .Q(Salida));  // open: en, clr
endmodule

module MBR (
  input  [7:0] Entrada_Memoria,
  input  LOAD_MBR,
  input  CLK,
  output [31:0] Salida_MBR_Signo,
  output [31:0] Salida_MBRU
);

  Registro_8_bits registro_8_bits_1 (
    .Entrada_Bus_C(Entrada_Memoria), .LOAD(LOAD_MBR), .CLK(CLK), .Salida(Salida_MBRU[7:0]));
  assign Salida_MBR_Signo = {{24{Salida_MBRU[7]}}, Salida_MBRU[7:0]};  // Bit_Extender bit_extender_1

  assign Salida_MBRU[31:8] = {24{1'b0}};
endmodule
